# Fritzing sketch Schema de montage (saved by Fritzing 0.9.3b)

parts:
  Composant1 = Arduino Mega 2560 (Rev3)
  Composant2 = RFID-RC522-v3
  X3 = X113647 Stepper Driver Board [part_number=X113647 package=board]
  MOTOR2 = 28BYJ-48 Stepper Motor
  Composant4 = Adafruit DS1307 RTC Breakout [part_number="Adafruit #264"]
  Composant6 = Bluetooth HC-05 Macho
  J1 = Basic Servo
  VCC1 = 4 x AAA Battery Mount
  M1 = fc-51 [package=THT]

nets:
  N1: Composant1.D21/SCL, Composant4.SQW, Composant4.SCL
  N2: Composant1.D20/SDA, Composant4.SDA
  N3: Composant1.D11_PWM, Composant6.RXD
  N4: Composant1.D10_PWM, Composant6.TXD
  N5: Composant1.D8_PWM, J1.pulse
  3V3: Composant1.3V3, Composant2.3.3V
  VCC: Composant1.5V, Composant4.VCC, Composant6.VCC, M1.pin3
  GND: Composant1.GND, Composant2.GND, Composant4.GND, Composant6.GND, M1.pin2
  N6: Composant1.D3_PWM, Composant2.RST
  N7: Composant1.D4_PWM, X3.IN1
  N8: Composant1.D5_PWM, X3.IN2
  N9: Composant1.D6_PWM, X3.IN3
  N10: Composant1.D7_PWM, X3.IN4
  N11: Composant1.D23, M1.pin1
  N12: Composant1.D50, Composant2.MISO
  N13: Composant1.D51, Composant2.MOSI
  N14: Composant1.D52, Composant2.SCK
  N15: Composant1.D53, Composant2.SDA
  GND_2: X3.GND, J1.gnd, VCC1.-
  N16: X3.+V, J1.vcc, VCC1.+
  N17: X3.BLUE, MOTOR2.BLUE
  N18: X3.PINK, MOTOR2.PINK
  N19: X3.YELLOW, MOTOR2.YELLOW
  N20: X3.ORANGE, MOTOR2.ORANGE
  N21: X3.RED, MOTOR2.RED

custom parts:
  RFID-RC522-v3: A simple China made RFID-RC522 Reader (6x4 cm); do check the pin labels, as this is a MFRC522 based clone.
  X113647 Stepper Driver Board: A common stepper motor driver board based on ULN2003APG darlington array
  Adafruit DS1307 RTC Breakout: This is a great battery-backed real time clock (RTC) that allows your microcontroller project to keep track of time even if it is reprogrammed, or if the power is lost. Perfect for datalogging, clock-building, time stamping, timers and alarms, etc. The DS1307 is the most popular RTC - but it requires 5V power to work (although we've used it with 5V power and 3.3V logic successfully) PCB &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
